# Fritzing sketch RGB_STM32 (saved by Fritzing 0.9.3b)
breadboards: 1

parts:
  R1 = Resistor [tolerance=±5% resistance=220 package=THT]
  R2 = Resistor [tolerance=±5% resistance=220 package=THT]
  R3 = Resistor [tolerance=±5% resistance=220 package=THT]
  J1 = STM32 Nucleo boards
  LED1 = RGB LED - (4 legs) [package="5 mm [THT]"]

nets:
  N1: R1.Pin_0, J1.PA5
  N2: R1.Pin_1, LED1.red_cathode
  N3: R2.Pin_0, J1.PA6
  N4: R2.Pin_1, LED1.green_cathode
  N5: R3.Pin_0, J1.PA7
  N6: R3.Pin_1, LED1.blue_cathode
  N7: J1.5V, LED1.common_anode
