# Fritzing sketch STM32_7SegDisp (saved by Fritzing 0.9.3b)
breadboards: 1

parts:
  DI1 = 7-Segment LED Display [package=THT]
  J1 = STM32 Nucleo boards

nets:
  N1: DI1.cathodeE, J1.PA4
  N2: DI1.cathodeD, J1.PA9
  N3: DI1.cathodeC, J1.PA8
  N4: DI1.cathodeB, J1.PA1
  N5: DI1.cathodeA, J1.PA0
  N6: DI1.commAnode#7, J1.5V
  N7: DI1.cathodeF, J1.PA5
  N8: DI1.cathodeG, J1.PA6
