# Fritzing sketch STM32_LCD (saved by Fritzing 0.9.3b)
breadboards: 1

parts:
  LCD1 = LCD screen
  J1 = STM32 Nucleo boards

nets:
  VSS: LCD1.VSS, LCD1.R/W, LCD1.LED-, J1.GND
  VDD: LCD1.VDD, LCD1.V0, LCD1.LED+, J1.5V
  N1: LCD1.RS, J1.D4
  N2: LCD1.E, J1.D5_PWM
  N3: LCD1.DB0, J1.D8
  N4: LCD1.DB1, J1.D11_PWM/MOSI
  N5: LCD1.DB2, J1.D12/MISO
  N6: LCD1.DB3, J1.D13/SCK
