# Fritzing sketch STM32_LDR (saved by Fritzing 0.9.3b)
breadboards: 1

parts:
  J1 = STM32 Nucleo boards
  R1 = Photocell (LDR) [package=THT]
  LED1 = smd LED [color="Red (633nm)" package="0805 [SMD]"]
  R2 = Resistor [tolerance=±5% resistance=220 package="0805 [SMD]"]

nets:
  N1: J1.A1, R1.pin_1, R2.Pin_0
  N2: J1.5V, R1.pin_0
  N3: J1.GND, LED1.cathode, R2.Pin_1
  N4: J1.PA6, LED1.anode
