# Fritzing sketch STM32_Pot (saved by Fritzing 0.9.3b)
breadboards: 1

parts:
  LED1 = smd LED [color="Red (633nm)" package="0805 [SMD]"]
  LED2 = smd LED [color="Red (633nm)" package="0805 [SMD]"]
  LED3 = smd LED [color="Red (633nm)" package="0805 [SMD]"]
  LED4 = smd LED [color="Red (633nm)" package="0805 [SMD]"]
  LED5 = smd LED [color="Red (633nm)" package="0805 [SMD]"]
  LED6 = smd LED [color="Red (633nm)" package="0805 [SMD]"]
  LED7 = smd LED [color="Red (633nm)" package="0805 [SMD]"]
  LED8 = smd LED [color="Red (633nm)" package="0805 [SMD]"]
  R1 = Rotary Potentiometer (Small) [maximum_resistance=100kΩ package=THT]
  J1 = STM32 Nucleo boards
  R2 = Resistor [tolerance=±5% resistance=220 package="0402 [SMD]"]
  R3 = Resistor [tolerance=±5% resistance=220 package="0402 [SMD]"]
  R4 = Resistor [tolerance=±5% resistance=220 package="0402 [SMD]"]
  R5 = Resistor [tolerance=±5% resistance=220 package="0402 [SMD]"]
  R6 = Resistor [tolerance=±5% resistance=220 package="0402 [SMD]"]
  R7 = Resistor [tolerance=±5% resistance=220 package="0402 [SMD]"]
  R8 = Resistor [tolerance=±5% resistance=220 package="0402 [SMD]"]
  R9 = Resistor [tolerance=±5% resistance=220 package="0402 [SMD]"]

nets:
  N1: LED1.cathode, LED2.cathode, LED3.cathode, LED4.cathode, LED5.cathode, LED6.cathode, LED7.cathode, LED8.cathode, R1.leg1, J1.GND
  N2: LED1.anode, R9.Pin_1
  N3: LED2.anode, R8.Pin_1
  N4: LED3.anode, R7.Pin_1
  N5: LED4.anode, R6.Pin_1
  N6: LED5.anode, R5.Pin_1
  N7: LED6.anode, R4.Pin_1
  N8: LED7.anode, R3.Pin_1
  N9: LED8.anode, R2.Pin_1
  N10: R1.wiper, J1.A0
  N11: R1.leg2, J1.5V
  N12: J1.PB8, R4.Pin_0
  N13: J1.PB9, R3.Pin_0
  N14: J1.PA5, R9.Pin_0
  N15: J1.PA6, R8.Pin_0
  N16: J1.PA7, R7.Pin_0
  N17: J1.PB6, R5.Pin_0
  N18: J1.PA8, R6.Pin_0
  N19: J1.PB10, R2.Pin_0
