# Fritzing sketch STM32_TwoButtons (saved by Fritzing 0.9.3b)
breadboards: 1

parts:
  LED1 = RGB LED (com. cathode, rbg) [package="5 mm [THT]"]
  S1 = Pushbutton [package="[SMD]"]
  J1 = STM32 Nucleo boards
  R1 = Resistor [tolerance=±5% resistance=220 package="0805 [SMD]"]
  R2 = Resistor [tolerance=±5% resistance=220 package="0805 [SMD]"]
  R3 = Resistor [tolerance=±5% resistance=220 package="0805 [SMD]"]
  R4 = Resistor [tolerance=±5% resistance=220 package="0805 [SMD]"]
  S2 = Pushbutton [package="[SMD]"]
  R5 = Resistor [tolerance=±5% resistance=220 package="0805 [SMD]"]

nets:
  N1: LED1.red_anode, R2.Pin_1
  N2: LED1.blue_anode, R3.Pin_1
  N3: LED1.green_anode, R4.Pin_1
  N4: S1.Pin_1, S1.Pin_2, J1.5V, S2.Pin_1, S2.Pin_2
  N5: S1.Pin_3, S1.Pin_4, J1.PA9, R1.Pin_0
  N6: J1.GND, R1.Pin_1, R5.Pin_1
  N7: J1.PA5, R2.Pin_0
  N8: J1.PA6, R3.Pin_0
  N9: J1.PA7, R4.Pin_0
  N10: J1.PA8, S2.Pin_3, S2.Pin_4, R5.Pin_0
